# Fritzing sketch XBeeGatewayRaspberryPi (saved by Fritzing 0.9.0b)
circuit board: 6.36939cm x 5.51965cm
breadboards: 1

parts:
  RSSI = LED - 3mm [color="Red (633nm)" package="3 mm [THT]"]
  Assc = LED - 3mm [color="Red (633nm)" package="3 mm [THT]"]
  XBee_Analog_Sensor_Board = XBee
  220 = Resistor [tolerance=±5% resistance=220 package=THT]
  220_2 = Resistor [tolerance=±5% resistance=220 package=THT]
  J1 = double row female pin header, 40 pins [form="♀ (female)"]

nets:
  N1: RSSI.anode, 220_2.Pin_0
  N2: Assc.anode, 220.Pin_0
  N3: XBee_Analog_Sensor_Board.VCC, J1.pin21
  N4: XBee_Analog_Sensor_Board.pin2, J1.pin16
  N5: XBee_Analog_Sensor_Board.pin3, J1.pin17
  N6: XBee_Analog_Sensor_Board.pin6, 220_2.Pin_1
  N7: XBee_Analog_Sensor_Board.pin15, 220.Pin_1

notes:
  Xbee RaspberryPi
  Design by tchap
  DIN
  DOUT
  VCC
  Gateway
