# Fritzing sketch XBeeSleepAnalogSensorBoard (saved by Fritzing 0.9.0b)
circuit board: 5.53245cm x 3.18788cm
breadboards: 1

parts:
  Attiny85 = attiny85 [package=dip]
  Actv = LED - 3mm [color="Red (633nm)" package="3 mm [THT]"]
  RSSI = LED - 3mm [color="Red (633nm)" package="3 mm [THT]"]
  Assc = LED - 3mm [color="Red (633nm)" package="3 mm [THT]"]
  XBee_Analog_Sensor_Board = XBee
  220 = Resistor [tolerance=±5% resistance=220 package=THT]
  220_2 = Resistor [tolerance=±5% resistance=220 package=THT]
  220_3 = Resistor [tolerance=±5% resistance=220 package=THT]
  JP1 = Header 2 [package=jst-2-pth]
  C1 = Tantalum Capacitor [capacitance=100nF package="100 mil [THT, tantalum]"]
  C2 = Electrolytic Capacitor [capacitance=10µF package="100 mil [THT, electrolytic]"]
  R1 = Resistor [tolerance=±5% resistance=220 package=THT]
  D1 = Zener Diode [part_number=1N4732A breakdown_voltage=3.6V package="300 mil [THT]"]
  JP3 = Header 3 [package=jst-3-pth]

nets:
  N1: Attiny85.Pin_1, R1.Pin_0
  N2: Attiny85.Pin_2, XBee_Analog_Sensor_Board.pin2
  N3: Attiny85.Pin_3, XBee_Analog_Sensor_Board.pin3
  N4: Attiny85.Pin_5, 220_3.Pin_0, JP3.2
  N5: Attiny85.Pin_6, XBee_Analog_Sensor_Board.pin9
  N6: Attiny85.Pin_7, JP3.1
  N7: Attiny85.Pin_8, XBee_Analog_Sensor_Board.VCC, C1.+, C2.+, R1.Pin_1, D1.cathode
  N8: Actv.anode, 220_3.Pin_1
  N9: RSSI.anode, 220_2.Pin_1
  N10: Assc.anode, 220.Pin_0
  N11: XBee_Analog_Sensor_Board.pin6, 220_2.Pin_0
  N12: XBee_Analog_Sensor_Board.pin15, 220.Pin_1
  N13: JP1.2, D1.anode

notes:
  based on a design by exsertus.com
  XBeeSensor85 v1.2b
  Xbee Sleep Analog Sensor Board
  1N4148
  10µF
  100nF
  10k
  Redesign by tchap
  - +
  SENSOR
  BAT
  - + SIG
  ATTINY85
